# Fritzing sketch lcm1602_DHT11 (saved by Fritzing 0.9.4)
breadboards: 1

parts:
  Εξάρτημα1 = Arduino Nano (Rev3.0)
  LCD2 = LCD screen
  LCM1602_IIC2 = LCM1602 IIC [part_number="LCM1602 IIC" chip_label="LCM1602 IIC" package="DIP (Dual Inline) [THT]"]
  DHT11_2 = DHT11 module
  J1 = Piezo Speaker

nets:
  GND: Εξάρτημα1.GND, LCM1602_IIC2.GND, J1.pin1
  N1: Εξάρτημα1.D2, DHT11_2.VCC
  N2: Εξάρτημα1.D4, J1.pin2
  N3: Εξάρτημα1.A5, LCM1602_IIC2.SCL
  N4: Εξάρτημα1.A4, LCM1602_IIC2.SDA
  3V3: Εξάρτημα1.3V3, LCM1602_IIC2.VCC, DHT11_2.DATA
  VSS: LCD2.VSS, LCM1602_IIC2.VSS
  VDD: LCD2.VDD, LCM1602_IIC2.VDD
  N5: LCD2.V0, LCM1602_IIC2.V0
  N6: LCD2.RS, LCM1602_IIC2.RS
  N7: LCD2.R/W, LCM1602_IIC2.RW
  N8: LCD2.E, LCM1602_IIC2.E
  N9: LCD2.DB0, LCM1602_IIC2.D0
  N10: LCD2.DB1, LCM1602_IIC2.D1
  N11: LCD2.DB2, LCM1602_IIC2.D2
  N12: LCD2.DB3, LCM1602_IIC2.D3
  N13: LCD2.DB4, LCM1602_IIC2.D4
  N14: LCD2.DB5, LCM1602_IIC2.D5
  N15: LCD2.DB6, LCM1602_IIC2.D6
  N16: LCD2.DB7, LCM1602_IIC2.D7
  N17: LCD2.LED+, LCM1602_IIC2.A
  N18: LCD2.LED-, LCM1602_IIC2.K
  N19: LCM1602_IIC2.LED_A, LCM1602_IIC2.LED_B

notes:
  arduino nano 33 iot
  1外部裝置只可以是小於或等於3.3V
  2輸出電壓為3.3V

custom parts:
  LCM1602 IIC: I2C-Module to use a 1602 or 2004 LCD on with the wire.h libory Serial LCD Modul
  DHT11 module: DHT11 black pcb module
