# Fritzing sketch sr04 (saved by Fritzing 0.9.4)
breadboards: 1

parts:
  Εξάρτημα1 = Arduino Nano (Rev3.0)
  HC-SR04_Sensor_1 = HC-SR04 Ultrasonic Distance Sensor
  S1 = Momentary Switch [package=ksa_sealed_tac_switch]

nets:
  GND: Εξάρτημα1.GND, HC-SR04_Sensor_1.GND, S1.4
  N1: Εξάρτημα1.D3, HC-SR04_Sensor_1.TRIG
  N2: Εξάρτημα1.D4, HC-SR04_Sensor_1.ECHO
  N3: Εξάρτημα1.D11/MOSI, S1.2
  5V: Εξάρτημα1.5V, HC-SR04_Sensor_1.VCC

notes:
  arduino nano 33 iot
  1外部裝置只可以是小於或等於3.3V
  2輸出電壓為3.3V
