# Fritzing sketch resistance (saved by Fritzing 0.9.3b)
breadboards: 1

parts:
  Εξάρτημα1 = Arduino Nano (Rev3.0)
  R1 = Rotary Potentiometer (Small) [maximum_resistance=100kΩ package=THT]

nets:
  N1: Εξάρτημα1.GND, R1.leg1
  N2: Εξάρτημα1.A0, R1.wiper
  N3: Εξάρτημα1.3V3, R1.leg2
